# Fritzing sketch Controller Monitor rev3 (saved by Fritzing 0.8.3b)
circuit board: 16.9333cm x 5.64444cm
perfboards: 1

parts:
  OLED1 = 128x64 Monochrom OLED Display with SPI Control
  DS1 = DS18B20 1-Wire Temperature Sensor [part_number=DS18B20]
  J1 = female pin header, 3 pins [form="♀ (female)"]
  DS3 = DS18B20 1-Wire Temperature Sensor [part_number=DS18B20]
  Part3 = Arduino Uno (Rev3)  # not connected
  Temp_+5V_/_Temp_Data = Screw terminal - 2 pins [package=THT]
  Veh_Gnd_/_Acc_+12V = Screw terminal - 2 pins [package=THT]
  Temp_Gnd_/_FTS_Gnd = Screw terminal - 2 pins [package=THT]
  FTS_S-Gnd_/_FTS_+28V = Screw terminal - 2 pins [package=THT]
  R5 = Resistor [tolerance=±1% resistance=200k package=THT]
  R6 = Resistor [tolerance=±1% resistance=1M package=THT]  # not connected
  DIP-Relay2 = DIP-Relay-D31A [part_number=R40-11D2-24]
  D2 = Rectifier Diode [part_number=1N4001 package="300 mil [THT]"]
  R7 = Resistor [tolerance=±5% resistance=4.7k package=THT]
  Q2 = NPN-Transistor [package="TO92 [THT]"]
  Part4 = Memoire 1.0 - SD card log shield
  S1 = Pushbutton [package="[THT]"]

nets:
  N1: OLED1.Data, Part4.DIG_11
  N2: OLED1.Clock, Part4.DIG_13
  N3: OLED1.SA0/DC, Part4.DIG_9
  N4: OLED1.Reset, Part4.DIG_7
  N5: OLED1.CS, Part4.DIG_8
  VIN: OLED1.Vin, Temp_+5V_/_Temp_Data.pin1, R7.Pin_1, Part4.+5V, S1.Pin_3, S1.Pin_4
  GND: OLED1.GND, Veh_Gnd_/_Acc_+12V.pin1, Temp_Gnd_/_FTS_Gnd.pin1, R5.Pin_1, Part4.GND
  VDD: DS1.VDD, J1.pin3, DS3.VDD
  N6: DS1.DQ, J1.pin2, DS3.DQ
  GND_2: DS1.GND, J1.pin1, DS3.GND
  N7: Temp_+5V_/_Temp_Data.pin2, R7.Pin_0, Part4.DIG_2
  N8: Veh_Gnd_/_Acc_+12V.pin2, Q2.C, Part4.VIN
  N9: Temp_Gnd_/_FTS_Gnd.pin2, DIP-Relay2.Coil2_-, DIP-Relay2.Coil_Sheeld
  N10: FTS_S-Gnd_/_FTS_+28V.pin1, DIP-Relay2.B1_Switch_Terminal_B
  N11: FTS_S-Gnd_/_FTS_+28V.pin2, DIP-Relay2.B2_Switch_Terminal_B
  N12: R5.Pin_0, Part4.A_IN_0
  N13: DIP-Relay2.A1_Switch_Terminal_A, D2.cathode
  N14: DIP-Relay2.A2_Switch_Terminal_A, D2.anode, Q2.E
  N15: Q2.B, Part4.DIG_4
  N16: Part4.DIG_3, S1.Pin_1, S1.Pin_2

notes:
  Daylight readable 128x64 OLED display
  Connected over Cat5
  DS18B20 Temp Sensors (Controller + Compressor)
  Sensors wrapped in heatshrink and taped to compontent in engine compartment
  30V - > 5V divider
  (1MΩ & 200kΩ)
  20 micro-amp draw
  DPDT Relay + Snubber Diode
  Dallas 1-wire 4.7kΩ pullup
  I'm using the slightly different Adafruit board, which has a 12x10 perfboard, approximated to the right
  Relay NPN transistor
  Legend
  White: Cat 5 (SPI)
  Red: +5V
  Purple: Digital Logic
  Brown: Analog
  Pink: +12V Vehicle Accessory
  FTS wires:
  Green: Ground
  Yellow: Switched Ground
  Striped Red: +28 - +17VDC
  Advanced Monitor, by Pug
  Phantom Full Throttle Supercharger
